# Fritzing sketch Sonar (saved by Fritzing 0.9.3b)
breadboards: 1

parts:
  Componente1 = Arduino Uno (Rev3)
  hc-sr1 = hc-sr04
  LED1 = smd LED [color="Red (633nm)" package="1206 [SMD]"]
  LED2 = smd LED [color="Green (565nm)" package="1206 [SMD]"]
  R1 = Resistor [tolerance=±5% resistance=220 package="0805 [SMD]"]
  R2 = Resistor [tolerance=±5% resistance=220 package="0402 [SMD]"]
  J1 = Basic Servo
  R3 = Resistor [tolerance=±5% resistance=220 package="0402 [SMD]"]
  J2 = Piezo Speaker

nets:
  N1: Componente1.D9_PWM, R3.Pin_0
  N2: Componente1.D2, R2.Pin_0
  N3: Componente1.D3_PWM, J1.pulse
  N4: Componente1.D4, hc-sr1.Trig
  N5: Componente1.D5_PWM, hc-sr1.Echo
  N6: Componente1.D6_PWM, R1.Pin_1
  VCC: Componente1.5V, hc-sr1.VCC, J1.vcc
  GND: Componente1.GND, hc-sr1.GND, LED1.cathode, LED2.cathode, J1.gnd, J2.pin1
  N7: LED1.anode, R1.Pin_0
  N8: LED2.anode, R2.Pin_1
  N9: R3.Pin_1, J2.pin2
